// Logisim project Logan8r.circ as structural Verilog: 2 circuits, main circuit main
module main (
);

  wire and_1_out, and_2_out, and_3_out, and_4_out, and_5_out, and_6_out, and_7_out, and_8_out, and_9_out,
       and_10_out, and_11_out, and_12_out, and_13_out, and_14_out, and_15_out, and_16_out, and_17_out,
       and_18_out, and_19_out, and_20_out, and_21_out, and_22_out, and_23_out, and_24_out, and_25_out,
       and_26_out, and_27_out, and_28_out, and_29_out, and_30_out, and_31_out, and_32_out, and_33_out,
       and_34_out, clk, d_ff_1_qn, DataClk, decoder_1_out0, decoder_1_out1, decoder_1_out2, decoder_1_out3,
       decoder_1_out4, decoder_1_out5, decoder_1_out6, decoder_1_out7, decoder_1_out8, decoder_1_out9,
       decoder_1_out10, decoder_1_out11, decoder_1_out12, decoder_1_out13, decoder_1_out14, decoder_1_out15,
       decoder_1_out16, decoder_1_out17, decoder_1_out18, decoder_1_out19, decoder_1_out20, decoder_1_out21,
       decoder_1_out22, decoder_1_out23, decoder_1_out24, decoder_1_out25, decoder_1_out26, decoder_1_out27,
       decoder_1_out28, decoder_1_out29, decoder_1_out30, decoder_1_out31;
  wire [1:0] led;
  wire [3:1] undriven, undriven_2;
  wire [4:0] ReadReg1, ReadReg2, WriteReg;
  wire [7:0] adder_1_out, adder_2_out, multiplexer_2_out, multiplexer_3_out, ram_2_dout, RegData1, RegData2,
       register_1_q, register_2_q, register_3_q, register_4_q, register_5_q, register_6_q, register_7_q,
       register_8_q, register_9_q, register_10_q, register_11_q, register_12_q, register_13_q, register_14_q,
       register_15_q, register_16_q, register_17_q, register_18_q, register_19_q, register_20_q,
       register_21_q, register_22_q, register_23_q, register_24_q, register_25_q, register_26_q,
       register_27_q, register_28_q, register_29_q, register_30_q, register_31_q, register_32_q,
       register_33_q, subtractor_1_out;
  wire [10:2] OPCODE;
  wire [15:10] ram_1_dout;
  wire [20:0] multiplexer_1_out;

  Register register_1 (.D(adder_1_out), .en(1'b1), .clk(clk), .Q(register_1_q));  // open: clr
  Adder adder_1 (.a(register_1_q), .b(8'h1), .out(adder_1_out));  // open: cin, cout
  RAM #(.dataWidth(32)) ram_1 (
    .addr(register_1_q), .we(1'b0), .oe(1'b1), .clk(clk),
    .dout({OPCODE, led, ReadReg2, ram_1_dout, ReadReg1, WriteReg}));  // open: din
  Multiplexer #(.select(2), .width(21)) multiplexer_1 (
    .in0(21'h1fee5c), .in1(21'h1fdf99), .in3(21'h7b498), .out(multiplexer_1_out), .sel(led));  // open: in2
  _7_Segment_Display u_7_segment_display_1 (
    .g(multiplexer_1_out[11]), .f(multiplexer_1_out[10]), .a(multiplexer_1_out[9]), .b(multiplexer_1_out[8]),
    .e(multiplexer_1_out[12]), .d(multiplexer_1_out[13]), .c(multiplexer_1_out[14]));  // open: dp
  _7_Segment_Display u_7_segment_display_2 (
    .g(multiplexer_1_out[7]), .f(multiplexer_1_out[6]), .a(multiplexer_1_out[5]), .b(multiplexer_1_out[4]),
    .e(multiplexer_1_out[15]), .d(multiplexer_1_out[16]), .c(multiplexer_1_out[17]));  // open: dp
  _7_Segment_Display u_7_segment_display_3 (
    .g(multiplexer_1_out[3]), .f(multiplexer_1_out[2]), .a(multiplexer_1_out[1]), .b(multiplexer_1_out[0]),
    .e(multiplexer_1_out[18]), .d(multiplexer_1_out[19]), .c(multiplexer_1_out[20]));  // open: dp
  _7_Segment_Display u_7_segment_display_4 (.g(1'b1), .e(1'b1));  // open: f, a, b, d, c, dp
  Hex_Digit_Display hex_digit_display_1 ();  // open: value, dp
  Adder adder_2 (.a(RegData2), .b(RegData1), .out(adder_2_out));  // open: cin, cout
  Subtractor subtractor_1 (.a(RegData1), .b(RegData2), .out(subtractor_1_out));  // open: bin, bout
  _7_Segment_Display u_7_segment_display_5 (.g(1'b1), .e(1'b1));  // open: f, a, b, d, c, dp
  Hex_Digit_Display hex_digit_display_2 (.value(WriteReg[3:0]));  // open: dp
  Multiplexer #(.select(2), .width(8)) multiplexer_2 (
    .in0(subtractor_1_out), .in1(adder_2_out), .in3(adder_2_out), .out(multiplexer_2_out), .sel(led));  // open: in2
  Hex_Digit_Display hex_digit_display_3 (.value({undriven, ReadReg1[4]}));  // open: dp
  and and_1 (and_1_out, led[0], and_2_out);
  and and_2 (and_2_out, led[0], led[1]);
  Hex_Digit_Display hex_digit_display_4 (.value(ReadReg1[3:0]));  // open: dp
  RAM ram_2 (.addr(multiplexer_2_out), .oe(and_1_out), .clk(DataClk), .dout(ram_2_dout));  // open: we, din
  _7_Segment_Display u_7_segment_display_6 (.g(1'b1), .e(1'b1));  // open: f, a, b, d, c, dp
  Hex_Digit_Display hex_digit_display_5 (.value({undriven_2, ReadReg2[4]}));  // open: dp
  Hex_Digit_Display hex_digit_display_6 (.value(ReadReg2[3:0]));  // open: dp
  Multiplexer #(.width(8)) multiplexer_3 (
    .in0(multiplexer_2_out), .in1(ram_2_dout), .out(multiplexer_3_out), .sel(and_1_out));
  Decoder #(.select(5)) decoder_1 (
    .out0(decoder_1_out0), .out1(decoder_1_out1), .out2(decoder_1_out2), .out3(decoder_1_out3),
    .out4(decoder_1_out4), .out5(decoder_1_out5), .out6(decoder_1_out6), .out7(decoder_1_out7),
    .out8(decoder_1_out8), .out9(decoder_1_out9), .out10(decoder_1_out10), .out11(decoder_1_out11),
    .out12(decoder_1_out12), .out13(decoder_1_out13), .out14(decoder_1_out14), .out15(decoder_1_out15),
    .out16(decoder_1_out16), .out17(decoder_1_out17), .out18(decoder_1_out18), .out19(decoder_1_out19),
    .out20(decoder_1_out20), .out21(decoder_1_out21), .out22(decoder_1_out22), .out23(decoder_1_out23),
    .out24(decoder_1_out24), .out25(decoder_1_out25), .out26(decoder_1_out26), .out27(decoder_1_out27),
    .out28(decoder_1_out28), .out29(decoder_1_out29), .out30(decoder_1_out30), .out31(decoder_1_out31),
    .sel(WriteReg), .en(1'b1));
  D_Flip_Flop d_ff_1 (.D(1'b1), .clk(clk), .Qn(d_ff_1_qn));  // open: Q, preset, reset
  and and_3 (and_3_out, decoder_1_out0, 1'b1);
  and and_4 (and_4_out, decoder_1_out1, 1'b1);
  and and_5 (and_5_out, decoder_1_out2, 1'b1);
  and and_6 (and_6_out, decoder_1_out3, 1'b1);
  and and_7 (and_7_out, decoder_1_out4, 1'b1);
  and and_8 (and_8_out, decoder_1_out5, 1'b1);
  and and_9 (and_9_out, decoder_1_out6, 1'b1);
  and and_10 (and_10_out, decoder_1_out7, 1'b1);
  and and_11 (and_11_out, decoder_1_out8, 1'b1);
  and and_12 (and_12_out, decoder_1_out9, 1'b1);
  and and_13 (and_13_out, decoder_1_out10, 1'b1);
  and and_14 (and_14_out, decoder_1_out11, 1'b1);
  and and_15 (and_15_out, decoder_1_out12, 1'b1);
  and and_16 (and_16_out, decoder_1_out13, 1'b1);
  and and_17 (and_17_out, decoder_1_out14, 1'b1);
  and and_18 (and_18_out, decoder_1_out15, 1'b1);
  and and_19 (and_19_out, decoder_1_out16, 1'b1);
  and and_20 (and_20_out, decoder_1_out17, 1'b1);
  and and_21 (and_21_out, decoder_1_out18, 1'b1);
  and and_22 (and_22_out, decoder_1_out19, 1'b1);
  and and_23 (and_23_out, decoder_1_out20, 1'b1);
  and and_24 (and_24_out, decoder_1_out21, 1'b1);
  and and_25 (and_25_out, decoder_1_out22, 1'b1);
  and and_26 (and_26_out, decoder_1_out23, 1'b1);
  and and_27 (and_27_out, decoder_1_out24, 1'b1);
  and and_28 (and_28_out, decoder_1_out25, 1'b1);
  and and_29 (and_29_out, decoder_1_out26, 1'b1);
  and and_30 (and_30_out, decoder_1_out27, 1'b1);
  and and_31 (and_31_out, decoder_1_out28, 1'b1);
  and and_32 (and_32_out, decoder_1_out29, 1'b1);
  and and_33 (and_33_out, decoder_1_out30, 1'b1);
  and and_34 (and_34_out, decoder_1_out31, 1'b1);
  Register register_2 (.D(multiplexer_3_out), .en(and_3_out), .clk(clk), .Q(register_2_q), .clr(d_ff_1_qn));
  Register register_3 (.D(multiplexer_3_out), .en(and_4_out), .clk(clk), .Q(register_3_q), .clr(d_ff_1_qn));
  Register register_4 (.D(multiplexer_3_out), .en(and_5_out), .clk(clk), .Q(register_4_q), .clr(d_ff_1_qn));
  Register register_5 (.D(multiplexer_3_out), .en(and_6_out), .clk(clk), .Q(register_5_q), .clr(d_ff_1_qn));
  Register register_6 (.D(multiplexer_3_out), .en(and_7_out), .clk(clk), .Q(register_6_q), .clr(d_ff_1_qn));
  Register register_7 (.D(multiplexer_3_out), .en(and_8_out), .clk(clk), .Q(register_7_q), .clr(d_ff_1_qn));
  Register register_8 (.D(multiplexer_3_out), .en(and_9_out), .clk(clk), .Q(register_8_q), .clr(d_ff_1_qn));
  Register register_9 (.D(multiplexer_3_out), .en(and_10_out), .clk(clk), .Q(register_9_q), .clr(d_ff_1_qn));
  Register register_10 (.D(multiplexer_3_out), .en(and_11_out), .clk(clk), .Q(register_10_q), .clr(d_ff_1_qn));
  Register register_11 (.D(multiplexer_3_out), .en(and_12_out), .clk(clk), .Q(register_11_q), .clr(d_ff_1_qn));
  Register register_12 (.D(multiplexer_3_out), .en(and_13_out), .clk(clk), .Q(register_12_q), .clr(d_ff_1_qn));
  Register register_13 (.D(multiplexer_3_out), .en(and_14_out), .clk(clk), .Q(register_13_q), .clr(d_ff_1_qn));
  Register register_14 (.D(multiplexer_3_out), .en(and_15_out), .clk(clk), .Q(register_14_q), .clr(d_ff_1_qn));
  Register register_15 (.D(multiplexer_3_out), .en(and_16_out), .clk(clk), .Q(register_15_q), .clr(d_ff_1_qn));
  Register register_16 (.D(multiplexer_3_out), .en(and_17_out), .clk(clk), .Q(register_16_q), .clr(d_ff_1_qn));
  Register register_17 (.D(multiplexer_3_out), .en(and_18_out), .clk(clk), .Q(register_17_q), .clr(d_ff_1_qn));
  Register register_18 (.D(multiplexer_3_out), .en(and_19_out), .clk(clk), .Q(register_18_q), .clr(d_ff_1_qn));
  Register register_19 (.D(multiplexer_3_out), .en(and_20_out), .clk(clk), .Q(register_19_q), .clr(d_ff_1_qn));
  Register register_20 (.D(multiplexer_3_out), .en(and_21_out), .clk(clk), .Q(register_20_q), .clr(d_ff_1_qn));
  Register register_21 (.D(multiplexer_3_out), .en(and_22_out), .clk(clk), .Q(register_21_q), .clr(d_ff_1_qn));
  Register register_22 (.D(multiplexer_3_out), .en(and_23_out), .clk(clk), .Q(register_22_q), .clr(d_ff_1_qn));
  Register register_23 (.D(multiplexer_3_out), .en(and_24_out), .clk(clk), .Q(register_23_q), .clr(d_ff_1_qn));
  Register register_24 (.D(multiplexer_3_out), .en(and_25_out), .clk(clk), .Q(register_24_q), .clr(d_ff_1_qn));
  Register register_25 (.D(multiplexer_3_out), .en(and_26_out), .clk(clk), .Q(register_25_q), .clr(d_ff_1_qn));
  Register register_26 (.D(multiplexer_3_out), .en(and_27_out), .clk(clk), .Q(register_26_q), .clr(d_ff_1_qn));
  Register register_27 (.D(multiplexer_3_out), .en(and_28_out), .clk(clk), .Q(register_27_q), .clr(d_ff_1_qn));
  Register register_28 (.D(multiplexer_3_out), .en(and_29_out), .clk(clk), .Q(register_28_q), .clr(d_ff_1_qn));
  Register register_29 (.D(multiplexer_3_out), .en(and_30_out), .clk(clk), .Q(register_29_q), .clr(d_ff_1_qn));
  Register register_30 (.D(multiplexer_3_out), .en(and_31_out), .clk(clk), .Q(register_30_q), .clr(d_ff_1_qn));
  Register register_31 (.D(multiplexer_3_out), .en(and_32_out), .clk(clk), .Q(register_31_q), .clr(d_ff_1_qn));
  Register register_32 (.D(multiplexer_3_out), .en(and_33_out), .clk(clk), .Q(register_32_q), .clr(d_ff_1_qn));
  Register register_33 (.D(multiplexer_3_out), .en(and_34_out), .clk(clk), .Q(register_33_q), .clr(d_ff_1_qn));
  Clock clock_1 (.out(DataClk));
  Clock #(.highDuration(2), .lowDuration(2)) clock_2 (.out(clk));
  Multiplexer #(.select(5), .width(8)) multiplexer_4 (
    .in0(register_2_q), .in1(register_3_q), .in2(register_4_q), .in3(register_5_q), .in4(register_6_q),
    .in5(register_7_q), .in6(register_8_q), .in7(register_9_q), .in8(register_10_q), .in9(register_11_q),
    .in10(register_12_q), .in11(register_13_q), .in12(register_14_q), .in13(register_15_q),
    .in14(register_16_q), .in15(register_17_q), .in16(register_18_q), .in17(register_19_q),
    .in18(register_20_q), .in19(register_21_q), .in20(register_22_q), .in21(register_23_q),
    .in22(register_24_q), .in23(register_25_q), .in24(register_26_q), .in25(register_27_q),
    .in26(register_28_q), .in27(register_29_q), .in28(register_30_q), .in29(register_31_q),
    .in30(register_32_q), .in31(register_33_q), .out(RegData1), .sel(ReadReg1));
  Multiplexer #(.select(5), .width(8)) multiplexer_5 (
    .in0(register_2_q), .in1(register_3_q), .in2(register_4_q), .in3(register_5_q), .in4(register_6_q),
    .in5(register_7_q), .in6(register_8_q), .in7(register_9_q), .in8(register_10_q), .in9(register_11_q),
    .in10(register_12_q), .in11(register_13_q), .in12(register_14_q), .in13(register_15_q),
    .in14(register_16_q), .in15(register_17_q), .in16(register_18_q), .in17(register_19_q),
    .in18(register_20_q), .in19(register_21_q), .in20(register_22_q), .in21(register_23_q),
    .in22(register_24_q), .in23(register_25_q), .in24(register_26_q), .in25(register_27_q),
    .in26(register_28_q), .in27(register_29_q), .in28(register_30_q), .in29(register_31_q),
    .in30(register_32_q), .in31(register_33_q), .out(RegData2), .sel(ReadReg2));

  // Other names for the same wires on the sheet: OPCODE[1:0] = led

  // Notes on the sheet:
  //   PC
  //   INSTRUCTION MEMORY
  //   Logan8r by Aidan Giordano and Alim Kassymov
  //   I pledge my honor that I have abided by the Stevens Honor System.
  //   ALU
  //   Logan8r
  //   ,
  //   CURRENT INSTRUCTION
  //   ,
  //   "We're in the endgame now."
  //   ,
  //   DATA MEMORY
  //   ,
  //   32 REGISTER BANK
  //   SYSTEM CLOCKS
  //   *Complete 1 Full Cycle To Power On CPU, then input register data
endmodule

module RegisterFile (
  input  [4:0] ReadReg1,
  input  [4:0] ReadReg2,
  input  [4:0] WriteReg,
  input  RegWrite,
  input  [7:0] RegDataW,
  input  clk,
  output [7:0] RegData1,
  output [7:0] RegData2
);

  wire and_1_out, and_2_out, and_3_out, and_4_out, and_5_out, and_6_out, and_7_out, and_8_out, and_9_out,
       and_10_out, and_11_out, and_12_out, and_13_out, and_14_out, and_15_out, and_16_out, and_17_out,
       and_18_out, and_19_out, and_20_out, and_21_out, and_22_out, and_23_out, and_24_out, and_25_out,
       and_26_out, and_27_out, and_28_out, and_29_out, and_30_out, and_31_out, and_32_out, decoder_1_out0,
       decoder_1_out1, decoder_1_out2, decoder_1_out3, decoder_1_out4, decoder_1_out5, decoder_1_out6,
       decoder_1_out7, decoder_1_out8, decoder_1_out9, decoder_1_out10, decoder_1_out11, decoder_1_out12,
       decoder_1_out13, decoder_1_out14, decoder_1_out15, decoder_1_out16, decoder_1_out17, decoder_1_out18,
       decoder_1_out19, decoder_1_out20, decoder_1_out21, decoder_1_out22, decoder_1_out23, decoder_1_out24,
       decoder_1_out25, decoder_1_out26, decoder_1_out27, decoder_1_out28, decoder_1_out29, decoder_1_out30,
       decoder_1_out31;
  wire [7:0] register_1_q, register_2_q, register_3_q, register_4_q, register_5_q, register_6_q,
       register_7_q, register_8_q, register_9_q, register_10_q, register_11_q, register_12_q, register_13_q,
       register_14_q, register_15_q, register_16_q, register_17_q, register_18_q, register_19_q,
       register_20_q, register_21_q, register_22_q, register_23_q, register_24_q, register_25_q,
       register_26_q, register_27_q, register_28_q, register_29_q, register_30_q, register_31_q,
       register_32_q;

  Decoder #(.select(5)) decoder_1 (
    .out0(decoder_1_out0), .out1(decoder_1_out1), .out2(decoder_1_out2), .out3(decoder_1_out3),
    .out4(decoder_1_out4), .out5(decoder_1_out5), .out6(decoder_1_out6), .out7(decoder_1_out7),
    .out8(decoder_1_out8), .out9(decoder_1_out9), .out10(decoder_1_out10), .out11(decoder_1_out11),
    .out12(decoder_1_out12), .out13(decoder_1_out13), .out14(decoder_1_out14), .out15(decoder_1_out15),
    .out16(decoder_1_out16), .out17(decoder_1_out17), .out18(decoder_1_out18), .out19(decoder_1_out19),
    .out20(decoder_1_out20), .out21(decoder_1_out21), .out22(decoder_1_out22), .out23(decoder_1_out23),
    .out24(decoder_1_out24), .out25(decoder_1_out25), .out26(decoder_1_out26), .out27(decoder_1_out27),
    .out28(decoder_1_out28), .out29(decoder_1_out29), .out30(decoder_1_out30), .out31(decoder_1_out31),
    .sel(WriteReg), .en(1'b1));
  and and_1 (and_1_out, decoder_1_out0, RegWrite);
  and and_2 (and_2_out, decoder_1_out1, RegWrite);
  and and_3 (and_3_out, decoder_1_out2, RegWrite);
  and and_4 (and_4_out, decoder_1_out3, RegWrite);
  and and_5 (and_5_out, decoder_1_out4, RegWrite);
  and and_6 (and_6_out, decoder_1_out5, RegWrite);
  and and_7 (and_7_out, decoder_1_out6, RegWrite);
  and and_8 (and_8_out, decoder_1_out7, RegWrite);
  and and_9 (and_9_out, decoder_1_out8, RegWrite);
  and and_10 (and_10_out, decoder_1_out9, RegWrite);
  and and_11 (and_11_out, decoder_1_out10, RegWrite);
  and and_12 (and_12_out, decoder_1_out11, RegWrite);
  and and_13 (and_13_out, decoder_1_out12, RegWrite);
  and and_14 (and_14_out, decoder_1_out13, RegWrite);
  and and_15 (and_15_out, decoder_1_out14, RegWrite);
  and and_16 (and_16_out, decoder_1_out15, RegWrite);
  and and_17 (and_17_out, decoder_1_out16, RegWrite);
  and and_18 (and_18_out, decoder_1_out17, RegWrite);
  and and_19 (and_19_out, decoder_1_out18, RegWrite);
  and and_20 (and_20_out, decoder_1_out19, RegWrite);
  and and_21 (and_21_out, decoder_1_out20, RegWrite);
  and and_22 (and_22_out, decoder_1_out21, RegWrite);
  and and_23 (and_23_out, decoder_1_out22, RegWrite);
  and and_24 (and_24_out, decoder_1_out23, RegWrite);
  and and_25 (and_25_out, decoder_1_out24, RegWrite);
  and and_26 (and_26_out, decoder_1_out25, RegWrite);
  and and_27 (and_27_out, decoder_1_out26, RegWrite);
  and and_28 (and_28_out, decoder_1_out27, RegWrite);
  and and_29 (and_29_out, decoder_1_out28, RegWrite);
  and and_30 (and_30_out, decoder_1_out29, RegWrite);
  and and_31 (and_31_out, decoder_1_out30, RegWrite);
  and and_32 (and_32_out, decoder_1_out31, RegWrite);
  Register register_1 (.D(RegDataW), .en(and_1_out), .clk(clk), .Q(register_1_q));  // open: clr
  Register register_2 (.D(RegDataW), .en(and_2_out), .clk(clk), .Q(register_2_q));  // open: clr
  Register register_3 (.D(RegDataW), .en(and_3_out), .clk(clk), .Q(register_3_q));  // open: clr
  Register register_4 (.D(RegDataW), .en(and_4_out), .clk(clk), .Q(register_4_q));  // open: clr
  Register register_5 (.D(RegDataW), .en(and_5_out), .clk(clk), .Q(register_5_q));  // open: clr
  Register register_6 (.D(RegDataW), .en(and_6_out), .clk(clk), .Q(register_6_q));  // open: clr
  Register register_7 (.D(RegDataW), .en(and_7_out), .clk(clk), .Q(register_7_q));  // open: clr
  Register register_8 (.D(RegDataW), .en(and_8_out), .clk(clk), .Q(register_8_q));  // open: clr
  Register register_9 (.D(RegDataW), .en(and_9_out), .clk(clk), .Q(register_9_q));  // open: clr
  Register register_10 (.D(RegDataW), .en(and_10_out), .clk(clk), .Q(register_10_q));  // open: clr
  Register register_11 (.D(RegDataW), .en(and_11_out), .clk(clk), .Q(register_11_q));  // open: clr
  Register register_12 (.D(RegDataW), .en(and_12_out), .clk(clk), .Q(register_12_q));  // open: clr
  Register register_13 (.D(RegDataW), .en(and_13_out), .clk(clk), .Q(register_13_q));  // open: clr
  Register register_14 (.D(RegDataW), .en(and_14_out), .clk(clk), .Q(register_14_q));  // open: clr
  Register register_15 (.D(RegDataW), .en(and_15_out), .clk(clk), .Q(register_15_q));  // open: clr
  Register register_16 (.D(RegDataW), .en(and_16_out), .clk(clk), .Q(register_16_q));  // open: clr
  Register register_17 (.D(RegDataW), .en(and_17_out), .clk(clk), .Q(register_17_q));  // open: clr
  Register register_18 (.D(RegDataW), .en(and_18_out), .clk(clk), .Q(register_18_q));  // open: clr
  Register register_19 (.D(RegDataW), .en(and_19_out), .clk(clk), .Q(register_19_q));  // open: clr
  Register register_20 (.D(RegDataW), .en(and_20_out), .clk(clk), .Q(register_20_q));  // open: clr
  Register register_21 (.D(RegDataW), .en(and_21_out), .clk(clk), .Q(register_21_q));  // open: clr
  Register register_22 (.D(RegDataW), .en(and_22_out), .clk(clk), .Q(register_22_q));  // open: clr
  Register register_23 (.D(RegDataW), .en(and_23_out), .clk(clk), .Q(register_23_q));  // open: clr
  Register register_24 (.D(RegDataW), .en(and_24_out), .clk(clk), .Q(register_24_q));  // open: clr
  Register register_25 (.D(RegDataW), .en(and_25_out), .clk(clk), .Q(register_25_q));  // open: clr
  Register register_26 (.D(RegDataW), .en(and_26_out), .clk(clk), .Q(register_26_q));  // open: clr
  Register register_27 (.D(RegDataW), .en(and_27_out), .clk(clk), .Q(register_27_q));  // open: clr
  Register register_28 (.D(RegDataW), .en(and_28_out), .clk(clk), .Q(register_28_q));  // open: clr
  Register register_29 (.D(RegDataW), .en(and_29_out), .clk(clk), .Q(register_29_q));  // open: clr
  Register register_30 (.D(RegDataW), .en(and_30_out), .clk(clk), .Q(register_30_q));  // open: clr
  Register register_31 (.D(RegDataW), .en(and_31_out), .clk(clk), .Q(register_31_q));  // open: clr
  Register register_32 (.D(RegDataW), .en(and_32_out), .clk(clk), .Q(register_32_q));  // open: clr
  Multiplexer #(.select(5), .width(8)) multiplexer_1 (
    .in0(register_1_q), .in1(register_2_q), .in2(register_3_q), .in3(register_4_q), .in4(register_5_q),
    .in5(register_6_q), .in6(register_7_q), .in7(register_8_q), .in8(register_9_q), .in9(register_10_q),
    .in10(register_11_q), .in11(register_12_q), .in12(register_13_q), .in13(register_14_q),
    .in14(register_15_q), .in15(register_16_q), .in16(register_17_q), .in17(register_18_q),
    .in18(register_19_q), .in19(register_20_q), .in20(register_21_q), .in21(register_22_q),
    .in22(register_23_q), .in23(register_24_q), .in24(register_25_q), .in25(register_26_q),
    .in26(register_27_q), .in27(register_28_q), .in28(register_29_q), .in29(register_30_q),
    .in30(register_31_q), .in31(register_32_q), .out(RegData1), .sel(ReadReg1));
  Multiplexer #(.select(5), .width(8)) multiplexer_2 (
    .in0(register_1_q), .in1(register_2_q), .in2(register_3_q), .in3(register_4_q), .in4(register_5_q),
    .in5(register_6_q), .in6(register_7_q), .in7(register_8_q), .in8(register_9_q), .in9(register_10_q),
    .in10(register_11_q), .in11(register_12_q), .in12(register_13_q), .in13(register_14_q),
    .in14(register_15_q), .in15(register_16_q), .in16(register_17_q), .in17(register_18_q),
    .in18(register_19_q), .in19(register_20_q), .in20(register_21_q), .in21(register_22_q),
    .in22(register_23_q), .in23(register_24_q), .in24(register_25_q), .in25(register_26_q),
    .in26(register_27_q), .in27(register_28_q), .in28(register_29_q), .in29(register_30_q),
    .in30(register_31_q), .in31(register_32_q), .out(RegData2), .sel(ReadReg2));
endmodule
